# Fritzing sketch Projeto cofre arduino (saved by Fritzing 0.9.3b)
breadboards: 1

parts:
  Componente1 = Arduino Uno (Rev3)
  U2 = LCD-16X2 [package=lcd-8x2-kit]
  U4 = QRD1114 [package=qrd1114]

nets:
  N1: Componente1.D8, U2.DB1
  N2: Componente1.D9_PWM, U2.DB3
  N3: Componente1.D10_PWM/SS, U2.DB5
  N4: Componente1.D11_PWM/MOSI, U2.E
  N5: Componente1.D13/SCK, U2.RS
  N6: Componente1.D2, U4.C
  N7: Componente1.D3_PWM, U4.E
  3V3: Componente1.3V3, U2.VDD
  N8: Componente1.5V, U2.K, U4.A
  N9: Componente1.GND, U2.DB7, U4.K
